# Fritzing sketch wemos d1 aciona rele com wifi (saved by Fritzing 0.9.3b)

parts:
  WeMos_D1_R1 = WeMos D1 R2
  U1 = 2-Channel 5v Relay Shield [package=relay-2ch5v10a]

nets:
  N1: WeMos_D1_R1.D2, U1.IN2
  N2: WeMos_D1_R1.D3, U1.IN1
  GND: WeMos_D1_R1.GND, U1.GND
  3.3V: WeMos_D1_R1.3.3V, U1.VCC

custom parts:
  WeMos D1 R2: The D1 R2 is a mini wifi board based on the ESP-8266EX.
  2-Channel 5v Relay Shield: 2 Channel 5v Relay Shield w. 2x SPD-06VDC-SD-C
